// Logisim project brainprocessor-74hc.circ as structural Verilog: 7 circuits, main circuit main
module main (
);

  wire and_1_out, and_2_out, and_3_out, and_4_out, and_5_out, and_6_out, and_7_out, and_8_out, and_9_out,
       and_10_out, and_12_out, and_13_out, BRAC_D_nU, BUF_ZERO, CLK, comparator_1_eq, DEC_BRAC, DEC_IN,
       DEC_O_nC, DEC_OUT, DEC_SHIFT, demultiplexer_1_out0, demultiplexer_1_out1, demultiplexer_2_out0,
       demultiplexer_2_out1, demultiplexer_3_out0, demultiplexer_3_out1, demultiplexer_4_out0,
       demultiplexer_4_out1, demultiplexer_5_out0, demultiplexer_5_out1, FSM_CLEAR, FSM_LOAD, FSM_RUN,
       FSM_SKIPB, FSM_SKIPF, FSMN_SKIP, INREADY, instruction_decoder_1_inc_ndec,
       instruction_decoder_1_left__right, instruction_decoder_1_ncount, instruction_decoder_1_nshift,
       nand_1_out, nAR_RCO, nBRAC_CTEN, nBRAC_RCO, nFSM_CLEAR, nor_1_out, nor_2_out, nor_3_out, nor_4_out,
       nor_5_out, not_1_out, not_3_out, not_5_out, not_6_out, not_7_out, not_8_out, not_9_out, not_10_out,
       not_11_out, not_12_out, not_13_out, not_14_out, nRST, or_1_out, or_2_out, or_3_out, PC_D_nU, RST;
  wire [4:0] not_17_out;
  wire [6:0] bit_extender_1_out, keyboard_1_data;
  wire [7:0] bit_extender_2_out, BUF_q, pull_resistor_1_node, ram_1_data, rom_1_data;
  wire [11:0] AR_q, BRAC_q, PC_q;

  not not_1 (not_1_out, comparator_1_eq);
  and and_1 (and_1_out, not_1_out, nor_1_out);
  nor nor_1 (nor_1_out, FSM_LOAD, FSM_CLEAR, and_2_out);
  Counter #(.width(12), .max('hfff)) PC (
    .load(PC_D_nU), .count(and_1_out), .Q(PC_q), .clk(CLK), .clr(RST));  // open: D, carry
  Instruction_Decoder instruction_decoder_1 (
    .Run(FSM_RUN), .Instruction(rom_1_data), .Out(DEC_OUT), .In(DEC_IN),
    .nCount(instruction_decoder_1_ncount), .Inc_nDec(instruction_decoder_1_inc_ndec),
    .nShift(instruction_decoder_1_nshift), .Left__Right(instruction_decoder_1_left__right), .Brac(DEC_BRAC),
    .Open_nClose(DEC_O_nC));
  and and_2 (and_2_out, ~INREADY, DEC_IN);  // AND_Gate
  Register #(.width(5)) FSM (
    .D({not_17_out[4:3], PC_D_nU, not_17_out[1:0]}),
    .Q({FSM_RUN, FSM_LOAD, FSM_SKIPB, FSM_SKIPF, nFSM_CLEAR}), .clk(CLK), .clr(RST));  // open: en
  not not_2 (FSM_CLEAR, nFSM_CLEAR);
  not not_3 (not_3_out, instruction_decoder_1_inc_ndec);
  not not_4 (DEC_SHIFT, instruction_decoder_1_nshift);
  not not_5 (not_5_out, nFSM_CLEAR);
  ROM #(.addrWidth(12)) rom_1 (.addr(PC_q), .data(rom_1_data));  // open: sel
  Comparator comparator_1 (.a({8{1'b0}}), .b(rom_1_data), .eq(comparator_1_eq));  // open: gt, lt
  _74HC161__12_bit AR (
    .D({12{1'b0}}), .D_nU(nor_3_out), .nCTEN(nor_2_out), .nLOAD(nRST), .CLK(CLK), .nRCO(nAR_RCO), .Q(AR_q));
  nor nor_2 (nor_2_out, DEC_SHIFT, FSM_CLEAR);
  nor nor_3 (nor_3_out, instruction_decoder_1_left__right, FSM_CLEAR);
  // Probe on AR_q
  not not_6 (not_6_out, CLK);
  Pull_Resistor pull_resistor_1 (.node(pull_resistor_1_node));
  nand nand_1 (nand_1_out, not_8_out, or_1_out);
  not not_7 (not_7_out, FSM_LOAD);
  nor nor_4 (nor_4_out, FSM_CLEAR, DEC_IN);
  _74HC191__8_bit BUF (
    .D(pull_resistor_1_node), .D_nU(not_3_out), .nCTEN(instruction_decoder_1_ncount), .nLOAD(nand_1_out),
    .Q(BUF_q), .CLK(CLK));  // open: nRCO
  // Probe on BUF_q
  not not_8 (not_8_out, CLK);
  or or_1 (or_1_out, ~not_7_out, ~nor_4_out);  // OR_Gate
  not not_9 (not_9_out, nor_4_out);
  Demultiplexer #(.enable("false")) demultiplexer_1 (
    .out0(demultiplexer_1_out0), .out1(demultiplexer_1_out1), .in(DEC_BRAC), .sel(DEC_O_nC));
  RAM #(.addrWidth(12), .bus("asynch")) ram_1 (
    .addr(AR_q), .data(ram_1_data), .sel(not_6_out), .ld(FSM_LOAD));  // open: clr
  assign pull_resistor_1_node = not_10_out ? ram_1_data : 8'bz;  // Controlled_Buffer controlled_buffer_1
  not not_10 (not_10_out, not_9_out);
  assign ram_1_data = not_11_out ? BUF_q : 8'bz;  // Controlled_Buffer controlled_buffer_2
  not not_11 (not_11_out, FSM_LOAD);
  assign pull_resistor_1_node = not_12_out ? bit_extender_2_out : 8'bz;  // Controlled_Buffer controlled_buffer_3
  not not_12 (not_12_out, not_13_out);
  not not_13 (not_13_out, DEC_IN);
  Comparator comparator_2 (.a(BUF_q), .b({8{1'b0}}), .eq(BUF_ZERO));  // open: gt, lt
  Bit_Extender #(.out_width(7)) bit_extender_1 (.in(ram_1_data), .out(bit_extender_1_out));
  Demultiplexer #(.enable("false")) demultiplexer_2 (
    .out0(demultiplexer_2_out0), .out1(demultiplexer_2_out1), .in(DEC_BRAC), .sel(DEC_O_nC));
  and and_3 (and_3_out, demultiplexer_1_out1, BUF_ZERO);
  and and_4 (and_4_out, demultiplexer_1_out0, ~BUF_ZERO);  // AND_Gate
  Clock Clock (.out(CLK));
  Button Reset (.out(RST));
  not not_14 (not_14_out, nAR_RCO);
  and and_5 (and_5_out, ~nBRAC_RCO, ~BRAC_D_nU);  // AND_Gate
  Demultiplexer #(.disabled(0), .enable("false")) demultiplexer_3 (
    .out0(demultiplexer_3_out0), .out1(demultiplexer_3_out1), .in(not_5_out), .sel(not_14_out));
  Demultiplexer #(.disabled(0), .enable("false")) demultiplexer_4 (
    .out0(demultiplexer_4_out0), .out1(demultiplexer_4_out1), .in(FSM_SKIPF), .sel(and_5_out));
  Demultiplexer #(.disabled(0), .enable("false")) demultiplexer_5 (
    .out0(demultiplexer_5_out0), .out1(demultiplexer_5_out1), .in(FSM_SKIPB), .sel(and_5_out));
  nor nor_5 (nor_5_out, DEC_SHIFT, and_3_out, and_4_out);
  TTY tty_1 (.data(bit_extender_1_out), .clk(CLK), .we(DEC_OUT), .clr(RST));
  Keyboard keyboard_1 (.clk(CLK), .re(DEC_IN), .clr(RST), .avail(INREADY), .data(keyboard_1_data));
  not not_15 (nRST, RST);
  and and_6 (and_6_out, FSM_SKIPF, demultiplexer_2_out0);
  or or_2 (or_2_out, and_6_out, and_7_out);
  and and_7 (and_7_out, FSM_SKIPB, demultiplexer_2_out1);
  and and_8 (and_8_out, FSM_SKIPF, demultiplexer_2_out1);
  or or_3 (or_3_out, and_8_out, and_9_out);
  and and_9 (and_9_out, FSM_SKIPB, demultiplexer_2_out0);
  and and_10 (and_10_out, FSM_RUN, nor_5_out);
  and and_11 (not_17_out[3], FSM_RUN, DEC_SHIFT);
  and and_12 (and_12_out, FSM_RUN, and_3_out);
  and and_13 (and_13_out, FSM_RUN, and_4_out);
  // Probe on BRAC_q
  _74HC161__12_bit BRAC (
    .D({12{1'b0}}), .D_nU(BRAC_D_nU), .nCTEN(nBRAC_CTEN), .nLOAD(nRST), .CLK(CLK), .nRCO(nBRAC_RCO),
    .Q(BRAC_q));
  not not_16 (BRAC_D_nU, or_2_out);
  nor nor_6 (nBRAC_CTEN, or_2_out, or_3_out, FSMN_SKIP);
  or or_4 (not_17_out[1], demultiplexer_4_out0, and_12_out);
  or or_5 (PC_D_nU, demultiplexer_5_out0, and_13_out);
  or or_6 (not_17_out[4], demultiplexer_3_out1, demultiplexer_4_out1, demultiplexer_5_out1, FSM_LOAD, and_10_out);
  or or_7 (FSMN_SKIP, and_12_out, and_13_out);
  assign bit_extender_2_out = {{1{1'b0}}, keyboard_1_data};  // Bit_Extender bit_extender_2
  not not_17 (not_17_out[0], demultiplexer_3_out0);
  _74HC139 u_74hc139_1 ();  // open: A0, A1, nY0, nY1, nY2, nY3, nEN
  // XOR_Gate xor_1 is placed but not wired
  // XOR_Gate xor_2 is placed but not wired
  Register #(.width(3)) register_1 ();  // open: D, en, Q, clk, clr
  // XOR_Gate xor_3 is placed but not wired

  // Notes on the sheet:
  //   Clear RAM
  //   Skip forward
  //   Skip backward
  //   Load
  //   Run
  //   contents of rom_1 (hex, n*v repeats v):
  //   a 5b 54 68 69 73 20 70 72 6f 67 72 61 6d 20 70 72 69 6e 74 73 20 22 48 65 6c 6c 6f 2c 20 57 6f 72 6c
  //   64 21 22 5d a a 9*2b 5b 3e 8*2b 3c 2d 5d 3e 2e 3c 11*20 39 78 38 3d 37 32 10*20 48 a 9*2b 5b 3e 2b
  //   2b 2b 3c 2d 5d 3e 2b 2b 2e 15*20 37 32 70 39 78 33 70 32 3d 31 30 31 4*20 65 a 7*2b 2e 2e 27*20 31
  //   30 31 70 37 3d 31 30 38 7*20 6c 20 6c a 2b 2b 2b 2e 32*20 31 30 38 70 33 3d 31 31 31 7*20 6f a 3e
  //   5*2b 5b 3e 8*2b 3c 2d 5d 3e 4*2b 2e 11*20 35 78 38 70 34 3d 34 34 8*20 63 6f 6d 6d 61 a 3e 2b 2b 5b
  //   3c 6*2d 3e 2d 5d 3c 2e 20*20 34 34 6d 32 78 36 3d 33 32 7*20 73 70 61 63 65 a 3e 7*2b 5b 3e 6*2b 3c
  //   2d 5d 3e 5b 2d 3c 2b 2b 3e 5d 3c 2b 2b 2b 2e 4*20 37 78 36 78 32 70 33 3d 38 37 6*20 57 a 3c 3c 3c
  //   2e 48*20 6f a 2b 2b 2b 2e 32*20 31 31 31 70 33 3d 31 31 34 7*20 72 a 6*2d 2e 29*20 31 31 34 6d 36 3d
  //   31 30 38 7*20 6c a 8*2d 2e 27*20 31 30 38 6d 38 3d 31 30 30 7*20 64 a 3e 3e 2b 2e 32*20 33 32 70 31
  //   3d 33 33 9*20 65 78 63 6c 61 69 6d a
  //   ]
  //   [
  //   ]
  //   [
  //   LEFTOVERS
endmodule

// decd
module Instruction_Decoder (
  input  Run,
  input  [7:0] Instruction,
  output Out,
  output In,
  output nCount,
  output Inc_nDec,
  output nShift,
  output Left__Right,
  output Brac,
  output Open_nClose
);

  wire and_1_out, and_2_out, and_3_out, and_4_out, and_5_out, n74hc139_1_ny0, n74hc139_1_ny1, n74hc139_1_ny2,
       n74hc139_1_ny3, nand_1_out, nand_2_out, nand_3_out, nand_4_out, nand_5_out, not_1_out, not_2_out,
       not_3_out, not_4_out, xor_1_out;

  not not_1 (not_1_out, Instruction[5]);
  not not_2 (not_2_out, Instruction[6]);
  not not_3 (not_3_out, Instruction[7]);
  xor xor_1 (xor_1_out, Instruction[2], Instruction[1]);
  and and_1 (and_1_out, ~Instruction[6], ~not_1_out);  // AND_Gate
  and and_2 (and_2_out, ~not_2_out, ~Instruction[5]);  // AND_Gate
  nand nand_1 (nand_1_out, Instruction[3], not_3_out);
  nand nand_2 (nand_2_out, Instruction[2], and_1_out);
  nand nand_3 (nand_3_out, xor_1_out, and_1_out);
  nand nand_4 (nand_4_out, xor_1_out, and_2_out);
  _74HC139 u_74hc139_1 (
    .A0(Instruction[0]), .A1(Instruction[4]), .nY0(n74hc139_1_ny0), .nY1(n74hc139_1_ny1),
    .nY2(n74hc139_1_ny2), .nY3(n74hc139_1_ny3), .nEN(nand_1_out));
  and and_3 (and_3_out, ~n74hc139_1_ny0, ~nand_2_out);  // AND_Gate
  and and_4 (and_4_out, ~n74hc139_1_ny1, ~nand_3_out);  // AND_Gate
  and and_5 (and_5_out, ~n74hc139_1_ny2, ~nand_2_out);  // AND_Gate
  and and_6 (Brac, ~n74hc139_1_ny3, ~nand_4_out);  // AND_Gate
  and and_7 (Out, ~nand_5_out, ~not_4_out);  // AND_Gate
  nand nand_5 (nand_5_out, Run, and_3_out);
  not not_4 (not_4_out, Instruction[1]);
  and and_8 (In, ~nand_5_out, ~Instruction[1]);  // AND_Gate
  nand nand_6 (nCount, Run, and_4_out);
  nand nand_7 (nShift, Run, and_5_out);

  assign Inc_nDec = Instruction[1];
  assign Left__Right = Instruction[1];
  assign Open_nClose = Instruction[1];
endmodule

module _74HC191 (
  input  A,
  input  B,
  input  C,
  input  D,
  input  CLK,
  input  nLOAD,
  input  D_nU,
  input  nCTEN,
  output nRCO,
  output QA,
  output QB,
  output QC,
  output QD
);

  wire and_1_out, and_2_out, and_3_out, and_4_out, and_5_out, demultiplexer_1_out0, demultiplexer_1_out1,
       demultiplexer_2_out0, demultiplexer_2_out1, demultiplexer_3_out0, demultiplexer_3_out1,
       demultiplexer_4_out0, demultiplexer_4_out1, nand_1_out, nand_2_out, nand_3_out, nand_4_out,
       nand_5_out, nand_6_out, nand_7_out, nand_8_out, nand_9_out, nand_10_out, nand_11_out, nand_12_out,
       nand_13_out, nor_1_out, nor_2_out, nor_3_out, nor_4_out, nor_5_out, nor_6_out, not_1_out, not_2_out,
       not_3_out, not_4_out, not_5_out, not_6_out, not_7_out, not_8_out, not_9_out, t_ff_1_qn, t_ff_2_qn,
       t_ff_3_qn, t_ff_4_qn;

  not not_1 (not_1_out, nLOAD);
  not not_2 (not_2_out, D_nU);
  not not_3 (not_3_out, nCTEN);
  and and_1 (and_1_out, CLK, ~not_1_out);  // AND_Gate
  not not_4 (not_4_out, not_2_out);
  nand nand_1 (nand_1_out, not_4_out, not_5_out);
  not not_5 (not_5_out, D_nU);
  not not_6 (not_6_out, A);
  and and_2 (and_2_out, nand_1_out, not_3_out);
  T_Flip_Flop t_ff_1 (
    .clk(and_1_out), .T(and_2_out), .Q(QA), .Qn(t_ff_1_qn), .preset(demultiplexer_1_out0),
    .reset(demultiplexer_1_out1));  // open: en
  Demultiplexer #(.enable("false")) demultiplexer_1 (
    .out0(demultiplexer_1_out0), .out1(demultiplexer_1_out1), .in(not_1_out), .sel(not_6_out));
  nand nand_2 (nand_2_out, QA, not_2_out);
  nand nand_3 (nand_3_out, nand_2_out, nand_4_out);
  nand nand_4 (nand_4_out, t_ff_1_qn, D_nU);
  not not_7 (not_7_out, B);
  and and_3 (and_3_out, nand_3_out, not_3_out);
  Demultiplexer #(.enable("false")) demultiplexer_2 (
    .out0(demultiplexer_2_out0), .out1(demultiplexer_2_out1), .in(not_1_out), .sel(not_7_out));
  nand nand_5 (nand_5_out, not_2_out, nor_1_out);
  T_Flip_Flop t_ff_2 (
    .clk(and_1_out), .T(and_3_out), .Q(QB), .Qn(t_ff_2_qn), .preset(demultiplexer_2_out0),
    .reset(demultiplexer_2_out1));  // open: en
  nand nand_6 (nand_6_out, D_nU, nor_2_out);
  nor nor_1 (nor_1_out, t_ff_1_qn, t_ff_2_qn);
  nand nand_7 (nand_7_out, nand_5_out, nand_6_out);
  nor nor_2 (nor_2_out, QA, QB);
  not not_8 (not_8_out, C);
  and and_4 (and_4_out, nand_7_out, not_3_out);
  Demultiplexer #(.enable("false")) demultiplexer_3 (
    .out0(demultiplexer_3_out0), .out1(demultiplexer_3_out1), .in(not_1_out), .sel(not_8_out));
  nor nor_3 (nor_3_out, t_ff_1_qn, t_ff_2_qn, t_ff_3_qn);
  nand nand_8 (nand_8_out, not_2_out, nor_3_out);
  T_Flip_Flop t_ff_3 (
    .clk(and_1_out), .T(and_4_out), .Q(QC), .Qn(t_ff_3_qn), .preset(demultiplexer_3_out0),
    .reset(demultiplexer_3_out1));  // open: en
  nand nand_9 (nand_9_out, D_nU, nor_4_out);
  nor nor_4 (nor_4_out, QA, QB, QC);
  nand nand_10 (nand_10_out, nand_8_out, nand_9_out);
  and and_5 (and_5_out, nand_10_out, not_3_out);
  not not_9 (not_9_out, D);
  T_Flip_Flop t_ff_4 (
    .clk(and_1_out), .T(and_5_out), .Q(QD), .Qn(t_ff_4_qn), .preset(demultiplexer_4_out0),
    .reset(demultiplexer_4_out1));  // open: en
  Demultiplexer #(.enable("false")) demultiplexer_4 (
    .out0(demultiplexer_4_out0), .out1(demultiplexer_4_out1), .in(not_1_out), .sel(not_9_out));
  nor nor_5 (nor_5_out, t_ff_1_qn, t_ff_2_qn, t_ff_3_qn, t_ff_4_qn);
  nand nand_11 (nand_11_out, not_2_out, nor_5_out);
  nand nand_12 (nand_12_out, D_nU, nor_6_out);
  nor nor_6 (nor_6_out, QA, QB, QC, QD);
  nand nand_13 (nand_13_out, nand_11_out, nand_12_out);
  nand nand_14 (nRCO, nand_13_out, not_3_out);
endmodule

// 191
module _74HC191__4_bit (
  input  [3:0] D,
  input  nLOAD,
  input  D_nU,
  input  nCTEN,
  input  CLK,
  output nRCO,
  output [3:0] Q
);

  _74HC191 u_74hc191_1 (
    .CLK(CLK), .nLOAD(nLOAD), .D_nU(D_nU), .nCTEN(nCTEN), .A(D[0]), .B(D[1]), .C(D[2]), .D(D[3]), .QA(Q[0]),
    .QB(Q[1]), .QC(Q[2]), .QD(Q[3]), .nRCO(nRCO));
endmodule

// 191
module _74HC191__8_bit (
  input  [7:0] D,
  input  D_nU,
  input  nCTEN,
  input  nLOAD,
  input  CLK,
  output nRCO,
  output [7:0] Q
);

  wire n74hc191_4_bit_1_nrco;

  _74HC191__4_bit u_74hc191_4_bit_1 (
    .D(D[3:0]), .nLOAD(nLOAD), .D_nU(D_nU), .nCTEN(nCTEN), .nRCO(n74hc191_4_bit_1_nrco), .Q(Q[3:0]), .CLK(CLK));
  _74HC191__4_bit u_74hc191_4_bit_2 (
    .D(D[7:4]), .nLOAD(nLOAD), .D_nU(D_nU), .nCTEN(n74hc191_4_bit_1_nrco), .nRCO(nRCO), .Q(Q[7:4]), .CLK(CLK));
endmodule

// 191
module _74HC161__12_bit (
  input  [11:0] D,
  input  D_nU,
  input  nCTEN,
  input  nLOAD,
  input  CLK,
  output nRCO,
  output [11:0] Q
);

  wire n74hc191_4_bit_1_nrco, n74hc191_4_bit_2_nrco;

  _74HC191__4_bit u_74hc191_4_bit_1 (
    .D(D[3:0]), .nLOAD(nLOAD), .D_nU(D_nU), .nCTEN(nCTEN), .nRCO(n74hc191_4_bit_1_nrco), .Q(Q[3:0]), .CLK(CLK));
  _74HC191__4_bit u_74hc191_4_bit_2 (
    .D(D[7:4]), .nLOAD(nLOAD), .D_nU(D_nU), .nCTEN(n74hc191_4_bit_1_nrco), .nRCO(n74hc191_4_bit_2_nrco),
    .Q(Q[7:4]), .CLK(CLK));
  _74HC191__4_bit u_74hc191_4_bit_3 (
    .D(D[11:8]), .nLOAD(nLOAD), .D_nU(D_nU), .nCTEN(n74hc191_4_bit_2_nrco), .nRCO(nRCO), .Q(Q[11:8]),
    .CLK(CLK));
endmodule

// 139
module _74HC139 (
  input  A0,
  input  A1,
  input  nEN,
  output nY0,
  output nY1,
  output nY2,
  output nY3
);

  wire not_1_out, not_2_out, not_3_out;

  not not_1 (not_1_out, A0);
  not not_2 (not_2_out, A1);
  not not_3 (not_3_out, nEN);
  nand nand_1 (nY0, not_1_out, not_2_out, not_3_out);
  nand nand_2 (nY1, A0, not_2_out, not_3_out);
  nand nand_3 (nY2, not_1_out, A1, not_3_out);
  nand nand_4 (nY3, A0, A1, not_3_out);

  // Notes on the sheet:
  //   nEN: pull=down
endmodule
